# Fritzing sketch schematic (saved by Fritzing 0.9.3b)

parts:
  Raspberry_Pi_B_rev1 = Raspberry Pi B rev1
  S1 = Round Pushbutton
  J1 = Piezo Speaker

nets:
  N1: Raspberry_Pi_B_rev1.GND, S1.leg1, J1.pin1
  N2: Raspberry_Pi_B_rev1.GPIO_23, J1.pin2
  N3: Raspberry_Pi_B_rev1.GPIO_17, S1.leg0
